// Logisim project FPA.circ as structural Verilog: 1 circuit, main circuit main
module main (
  input  [31:0] A,
  input  [31:0] B,
  output overflow,
  output underflow,
  output [19:0] significand,
  output [10:0] exponent,
  output sign
);

  wire input_1_larger_s_sign, input_1_smaller_s_sign, normalizer_1_overflow, rounded_normalizer_1_overflow;
  wire [10:0] input_1_larger_exponent, normalizer_1_normalized_exponent;
  wire [31:0] adder32bit_1_out_6, input_1_larger_s_fraction, input_1_shifted_smaller_s_fraction,
       normalizer_1_normalized_significand, rounded_normalizer_1_normalized_significand,
       rounder_1_rounded_significand;
  wire [31:31] adder32bit_1_carry_out;

  Input input_1 (
    .A(A), .B(B), .Larger_s_Fraction(input_1_larger_s_fraction), .Larger_s_Sign(input_1_larger_s_sign),
    .Larger_Exponent(input_1_larger_exponent),
    .Shifted_Smaller_s_Fraction(input_1_shifted_smaller_s_fraction), .Smaller_s_sign(input_1_smaller_s_sign));  // open: Exponent_Difference, Smaller_s_Fraction
  adder32bit adder32bit_1 (
    .sign_A(input_1_larger_s_sign), .A(input_1_larger_s_fraction), .B(input_1_shifted_smaller_s_fraction),
    .sign_B(input_1_smaller_s_sign), .Carry_Out(adder32bit_1_carry_out[31]), .out_6(adder32bit_1_out_6),
    .Output_Sign(sign));
  normalizer normalizer_1 (
    .exponent_input(input_1_larger_exponent),
    .significand_input({adder32bit_1_carry_out[31], adder32bit_1_out_6[31:1]}), .underflow(underflow),
    .overflow(normalizer_1_overflow), .normalized_Exponent(normalizer_1_normalized_exponent),
    .normalized_Significand(normalizer_1_normalized_significand));
  Rounder rounder_1 (
    .significand(normalizer_1_normalized_significand), .rounded_significand(rounder_1_rounded_significand));
  rounded_normalizer rounded_normalizer_1 (
    .exponent_input(normalizer_1_normalized_exponent), .significand_input(rounder_1_rounded_significand),
    .overflow(rounded_normalizer_1_overflow), .normalized_Exponent(exponent),
    .normalized_Significand({rounded_normalizer_1_normalized_significand[31:30], significand, rounded_normalizer_1_normalized_significand[9:0]}));
  or or_1 (overflow, rounded_normalizer_1_overflow, normalizer_1_overflow);
endmodule
