// Logisim project adder32bit.circ as structural Verilog: 1 circuit, main circuit adder32bit
// ADD
module adder32bit (
  input  sign_A,
  input  [31:0] A,
  input  [31:0] B,
  input  sign_B,
  output Carry_Out,
  output [31:0] out_6,
  output Output_Sign
);

  wire comparator_1_eq, comparator_1_lt, multiplexer_3_out, multiplexer_4_out, xor_1_out, xor_2_out;
  wire [31:0] adder_1_out, multiplexer_1_out, negator_1_out, subtractor_1_out;

  xor xor_1 (xor_1_out, sign_A, sign_B);
  Adder #(.width(32)) adder_1 (.a(A), .b(B), .out(adder_1_out), .cin(1'b0), .cout(Carry_Out));
  Subtractor #(.width(32)) subtractor_1 (.a(A), .b(B), .out(subtractor_1_out));  // open: bin, bout
  Comparator #(.width(32)) comparator_1 (.a(A), .b(B), .eq(comparator_1_eq), .lt(comparator_1_lt));  // open: gt
  Negator #(.width(32)) negator_1 (.in(subtractor_1_out), .out(negator_1_out));
  Multiplexer #(.width(32), .disabled(0), .enable("false")) multiplexer_1 (
    .in0(subtractor_1_out), .in1(negator_1_out), .out(multiplexer_1_out), .sel(comparator_1_lt));
  Multiplexer #(.width(32), .disabled(0), .enable("false")) multiplexer_2 (
    .in0(adder_1_out), .in1(multiplexer_1_out), .out(out_6), .sel(xor_1_out));
  Multiplexer #(.disabled(0), .enable("false")) multiplexer_3 (
    .in0(sign_A), .in1(sign_B), .out(multiplexer_3_out), .sel(comparator_1_lt));
  Multiplexer #(.disabled(0), .enable("false")) multiplexer_4 (
    .in0(multiplexer_3_out), .in1(1'b0), .out(multiplexer_4_out), .sel(comparator_1_eq));
  xor xor_2 (xor_2_out, xor_1_out, sign_B);
  Multiplexer #(.disabled(0), .enable("false")) multiplexer_5 (
    .in0(xor_2_out), .in1(multiplexer_4_out), .out(Output_Sign), .sel(xor_1_out));
endmodule
