// Logisim project normalizer.circ as structural Verilog: 3 circuits, main circuit normalizer
// NMR
module normalizer (
  input  [10:0] exponent_input,
  input  [31:0] significand_input,
  output [10:0] normalized_Exponent,
  output [31:0] normalized_Significand
);

  wire and_1_out, priority_encoder_1_en_out, xor_1_out;
  wire [4:0] multiplexer_1_out, priority_encoder_1_out, subtractor_1_out;
  wire [10:0] adder_substractorlib_1_out_4;
  wire [31:0] shifter_1_output;

  xor xor_1 (xor_1_out, significand_input[31], 1'b1);
  and and_1 (and_1_out, xor_1_out, priority_encoder_1_en_out);
  Priority_Encoder #(.select(5)) priority_encoder_1 (
    .in0(significand_input[0]), .in1(significand_input[1]), .in2(significand_input[2]),
    .in3(significand_input[3]), .in4(significand_input[4]), .in5(significand_input[5]),
    .in6(significand_input[6]), .in7(significand_input[7]), .in8(significand_input[8]),
    .in9(significand_input[9]), .in10(significand_input[10]), .in11(significand_input[11]),
    .in12(significand_input[12]), .in13(significand_input[13]), .in14(significand_input[14]),
    .in15(significand_input[15]), .in16(significand_input[16]), .in17(significand_input[17]),
    .in18(significand_input[18]), .in19(significand_input[19]), .in20(significand_input[20]),
    .in21(significand_input[21]), .in22(significand_input[22]), .in23(significand_input[23]),
    .in24(significand_input[24]), .in25(significand_input[25]), .in26(significand_input[26]),
    .in27(significand_input[27]), .in28(significand_input[28]), .in29(significand_input[29]),
    .in30(significand_input[30]), .in31(1'b0), .out(priority_encoder_1_out),
    .en_out(priority_encoder_1_en_out), .en_in(1'b1));  // open: gs
  Shifter shifter_1 (
    .\input (significand_input), .shiftAmmount(multiplexer_1_out), .left_right(significand_input[31]),
    .\output (shifter_1_output));
  Subtractor #(.width(5)) subtractor_1 (
    .a(5'b11110), .b(priority_encoder_1_out), .out(subtractor_1_out));  // open: bin, bout
  Multiplexer #(.width(5), .disabled(0), .enable("false")) multiplexer_1 (
    .in0(subtractor_1_out), .in1(5'b00001), .out(multiplexer_1_out), .sel(significand_input[31]));
  Multiplexer #(.width(11), .disabled(0), .enable("false")) multiplexer_2 (
    .in0(adder_substractorlib_1_out_4), .in1({11{1'b0}}), .out(normalized_Exponent), .sel(and_1_out));
  Multiplexer #(.width(32), .disabled(0), .enable("false")) multiplexer_3 (
    .in0(shifter_1_output), .in1({32{1'b0}}), .out(normalized_Significand), .sel(and_1_out));
  adder_substractorLib adder_substractorlib_1 (
    .input1(exponent_input), .input2(multiplexer_1_out), .add_sub(significand_input[31]),
    .out_4(adder_substractorlib_1_out_4));

  // Notes on the sheet:
  //   encoded value
  //   highest encoded value
  //   substractor
  //   right shift ammount
endmodule

// shifter
module Shifter (
  input  [31:0] \input ,
  input  [4:0] shiftAmmount,
  input  left_right,
  output [31:0] \output 
);

  wire [31:0] arbitary_rightshifter_1_p3, arbitrary_leftshifter_1_p3;

  // arbitrary_leftShifter arbitrary_leftshifter_1: pin names not known; wires that end beside it: \input , shiftAmmount, arbitrary_leftshifter_1_p3
  // arbitary_rightShifter arbitary_rightshifter_1: pin names not known; wires that end beside it: \input , shiftAmmount, arbitary_rightshifter_1_p3
  Multiplexer #(.width(32), .disabled(0), .enable("false")) multiplexer_1 (
    .in0(arbitrary_leftshifter_1_p3), .in1(arbitary_rightshifter_1_p3), .out(\output ), .sel(left_right));
endmodule

// A/S
module adder_substractorLib (
  input  [10:0] input1,
  input  [4:0] input2,
  input  add_sub,
  output [10:0] out_4
);

  wire [10:0] adder_1_out, multiplexer_1_out, negator_1_out, subtractor_1_out, undriven;

  Subtractor #(.width(11)) subtractor_1 (
    .a(input1), .b({{6{1'b0}}, input2}), .out(subtractor_1_out), .bin(1'b0));  // open: bout
  Adder #(.width(11)) adder_1 (.a(input1), .b({{6{1'b0}}, input2}), .out(adder_1_out), .cin(1'b0));  // open: cout
  Negator #(.width(11)) negator_1 (.out(negator_1_out));  // open: in
  Multiplexer #(.width(11), .disabled(0), .enable("false")) multiplexer_1 (
    .in0(undriven), .in1(negator_1_out), .out(multiplexer_1_out));  // open: sel
  Multiplexer #(.width(11), .disabled(0), .enable("false")) multiplexer_2 (
    .in0(subtractor_1_out), .in1(adder_1_out), .out(out_4), .sel(add_sub));
endmodule
